// Logisim project FP_adder.circ as structural Verilog: 10 circuits, main circuit main
module main (
  input  [15:0] A,
  input  [15:0] B,
  output Overflow,
  output Underflow,
  output [15:0] Result
);

  FP_adder fp_adder_1 (.Operand_A(A), .Operand_B(B), .Result(Result), .Underflow(Underflow), .Overflow(Overflow));
endmodule

// ALU 0
module _1_Bit_ALU (
  input  Operand_B,
  input  Operand_A,
  input  Carry_In,
  input  Binvert,
  input  [1:0] Operation,
  output Result0,
  output Carry0
);

  wire adder_1_out, and_1_out, multiplexer_1_out, not_1_out, or_1_out;

  not not_1 (not_1_out, Operand_B);
  Multiplexer multiplexer_1 (.in0(Operand_B), .in1(not_1_out), .out(multiplexer_1_out), .sel(Binvert));  // open: en
  and and_1 (and_1_out, Operand_A, multiplexer_1_out);
  or or_1 (or_1_out, Operand_A, multiplexer_1_out);
  Adder #(.width(1)) adder_1 (.a(Operand_A), .b(multiplexer_1_out), .out(adder_1_out), .cin(Carry_In), .cout(Carry0));
  Multiplexer #(.select(2)) multiplexer_2 (
    .in0(and_1_out), .in1(or_1_out), .in2(adder_1_out), .out(Result0), .sel(Operation));  // open: in3, en
endmodule

module _4_bit_ALU (
  input  [3:0] A,
  input  CarryIn,
  input  AInvert,
  input  [3:0] B,
  input  BInvert,
  input  [1:0] Operation,
  input  A_B,
  output [3:0] Exp__Difff,
  output Zero,
  output Overflow,
  output Carry
);

  wire n1_bit_alu_1_carry0, n1_bit_alu_2_carry0, n1_bit_alu_3_carry0;
  wire [3:0] adder_1_out, adder_2_out, multiplexer_1_out, multiplexer_2_out, n1_bit_alu_1_result0, not_5_out,
       not_6_out;

  not not_1 (not_5_out[2], A[2]);
  not not_2 (not_5_out[1], A[1]);
  not not_3 (not_5_out[3], A[3]);
  not not_4 (not_6_out[3], B[3]);
  not not_5 (not_5_out[0], A[0]);
  Adder #(.width(4)) adder_1 (.a(not_5_out), .b(4'b0001), .out(adder_1_out), .cin(1'b0));  // open: cout
  not not_6 (not_6_out[0], B[0]);
  not not_7 (not_6_out[2], B[2]);
  not not_8 (not_6_out[1], B[1]);
  Multiplexer #(.width(4), .enable("false")) multiplexer_1 (
    .in0(A), .in1(adder_1_out), .out(multiplexer_1_out), .sel(AInvert));
  Multiplexer #(.width(4), .enable("false")) multiplexer_2 (
    .in0(B), .in1(adder_2_out), .out(multiplexer_2_out), .sel(BInvert));
  Adder #(.width(4)) adder_2 (.a(not_6_out), .b(4'b0001), .out(adder_2_out), .cin(1'b0));  // open: cout
  _1_Bit_ALU u_1_bit_alu_1 (
    .Result0(n1_bit_alu_1_result0[0]), .Carry0(n1_bit_alu_1_carry0), .Operand_B(multiplexer_2_out[0]),
    .Operand_A(multiplexer_1_out[0]), .Binvert(1'b0), .Operation(Operation), .Carry_In(CarryIn));
  _1_Bit_ALU u_1_bit_alu_2 (
    .Result0(n1_bit_alu_1_result0[1]), .Carry0(n1_bit_alu_2_carry0), .Operand_B(multiplexer_2_out[1]),
    .Operand_A(multiplexer_1_out[1]), .Binvert(1'b0), .Operation(Operation), .Carry_In(n1_bit_alu_1_carry0));
  _1_Bit_ALU u_1_bit_alu_3 (
    .Result0(n1_bit_alu_1_result0[2]), .Carry0(n1_bit_alu_3_carry0), .Operand_B(multiplexer_2_out[2]),
    .Operand_A(multiplexer_1_out[2]), .Binvert(1'b0), .Operation(Operation), .Carry_In(n1_bit_alu_2_carry0));
  _1_Bit_ALU u_1_bit_alu_4 (
    .Result0(n1_bit_alu_1_result0[3]), .Carry0(Carry), .Operand_B(multiplexer_2_out[3]),
    .Operand_A(multiplexer_1_out[3]), .Binvert(1'b0), .Operation(Operation), .Carry_In(n1_bit_alu_3_carry0));
  xor xor_1 (Overflow, n1_bit_alu_3_carry0, Carry);
  Multiplexer #(.width(4), .enable("false")) multiplexer_3 (
    .in0(n1_bit_alu_1_result0), .in1(4'b0000), .out(Exp__Difff), .sel(A_B));
  nor nor_1 (Zero, n1_bit_alu_1_result0[0], n1_bit_alu_1_result0[1], n1_bit_alu_1_result0[2], n1_bit_alu_1_result0[3]);
endmodule

module _16_bit_ALU (
  input  CarryIn,
  input  [15:0] Operand_A,
  input  [15:0] Operand_B,
  input  [1:0] Operation,
  input  Binvert,
  input  A_B,
  output zero,
  output [15:0] result,
  output Carry15,
  output Overflow
);

  wire and_1_out, n1_bit_alu_1_carry0, n1_bit_alu_2_carry0, n1_bit_alu_3_carry0, n1_bit_alu_4_carry0,
       n1_bit_alu_5_carry0, n1_bit_alu_6_carry0, n1_bit_alu_7_carry0, n1_bit_alu_8_carry0,
       n1_bit_alu_9_carry0, n1_bit_alu_10_carry0, n1_bit_alu_11_carry0, n1_bit_alu_12_carry0,
       n1_bit_alu_13_carry0, n1_bit_alu_14_carry0, n1_bit_alu_15_carry0;
  wire [15:0] n1_bit_alu_1_result0;

  and and_1 (and_1_out, A_B, Operand_B[15]);
  _1_Bit_ALU u_1_bit_alu_1 (
    .Result0(n1_bit_alu_1_result0[0]), .Carry0(n1_bit_alu_1_carry0), .Operand_B(Operand_B[0]),
    .Operand_A(Operand_A[0]), .Binvert(Binvert), .Operation(Operation), .Carry_In(CarryIn));
  _1_Bit_ALU u_1_bit_alu_2 (
    .Result0(n1_bit_alu_1_result0[1]), .Carry0(n1_bit_alu_2_carry0), .Operand_B(Operand_B[1]),
    .Operand_A(Operand_A[1]), .Binvert(Binvert), .Operation(Operation), .Carry_In(n1_bit_alu_1_carry0));
  _1_Bit_ALU u_1_bit_alu_3 (
    .Result0(n1_bit_alu_1_result0[2]), .Carry0(n1_bit_alu_3_carry0), .Operand_B(Operand_B[2]),
    .Operand_A(Operand_A[2]), .Binvert(Binvert), .Operation(Operation), .Carry_In(n1_bit_alu_2_carry0));
  _1_Bit_ALU u_1_bit_alu_4 (
    .Result0(n1_bit_alu_1_result0[3]), .Carry0(n1_bit_alu_4_carry0), .Operand_B(Operand_B[3]),
    .Operand_A(Operand_A[3]), .Binvert(Binvert), .Operation(Operation), .Carry_In(n1_bit_alu_3_carry0));
  _1_Bit_ALU u_1_bit_alu_5 (
    .Result0(n1_bit_alu_1_result0[4]), .Carry0(n1_bit_alu_5_carry0), .Operand_B(Operand_B[4]),
    .Operand_A(Operand_A[4]), .Binvert(Binvert), .Operation(Operation), .Carry_In(n1_bit_alu_4_carry0));
  _1_Bit_ALU u_1_bit_alu_6 (
    .Result0(n1_bit_alu_1_result0[5]), .Carry0(n1_bit_alu_6_carry0), .Operand_B(Operand_B[5]),
    .Operand_A(Operand_A[5]), .Binvert(Binvert), .Operation(Operation), .Carry_In(n1_bit_alu_5_carry0));
  _1_Bit_ALU u_1_bit_alu_7 (
    .Result0(n1_bit_alu_1_result0[6]), .Carry0(n1_bit_alu_7_carry0), .Operand_B(Operand_B[6]),
    .Operand_A(Operand_A[6]), .Binvert(Binvert), .Operation(Operation), .Carry_In(n1_bit_alu_6_carry0));
  _1_Bit_ALU u_1_bit_alu_8 (
    .Result0(n1_bit_alu_1_result0[7]), .Carry0(n1_bit_alu_8_carry0), .Operand_B(Operand_B[7]),
    .Operand_A(Operand_A[7]), .Binvert(Binvert), .Operation(Operation), .Carry_In(n1_bit_alu_7_carry0));
  _1_Bit_ALU u_1_bit_alu_9 (
    .Result0(n1_bit_alu_1_result0[8]), .Carry0(n1_bit_alu_9_carry0), .Operand_B(Operand_B[8]),
    .Operand_A(Operand_A[8]), .Binvert(Binvert), .Operation(Operation), .Carry_In(n1_bit_alu_8_carry0));
  _1_Bit_ALU u_1_bit_alu_10 (
    .Result0(n1_bit_alu_1_result0[9]), .Carry0(n1_bit_alu_10_carry0), .Operand_B(Operand_B[9]),
    .Operand_A(Operand_A[9]), .Binvert(Binvert), .Operation(Operation), .Carry_In(n1_bit_alu_9_carry0));
  _1_Bit_ALU u_1_bit_alu_11 (
    .Result0(n1_bit_alu_1_result0[10]), .Carry0(n1_bit_alu_11_carry0), .Operand_B(Operand_B[10]),
    .Operand_A(Operand_A[10]), .Binvert(Binvert), .Operation(Operation), .Carry_In(n1_bit_alu_10_carry0));
  _1_Bit_ALU u_1_bit_alu_12 (
    .Result0(n1_bit_alu_1_result0[11]), .Carry0(n1_bit_alu_12_carry0), .Operand_B(Operand_B[11]),
    .Operand_A(Operand_A[11]), .Binvert(Binvert), .Operation(Operation), .Carry_In(n1_bit_alu_11_carry0));
  _1_Bit_ALU u_1_bit_alu_13 (
    .Result0(n1_bit_alu_1_result0[12]), .Carry0(n1_bit_alu_13_carry0), .Operand_B(Operand_B[12]),
    .Operand_A(Operand_A[12]), .Binvert(Binvert), .Operation(Operation), .Carry_In(n1_bit_alu_12_carry0));
  _1_Bit_ALU u_1_bit_alu_14 (
    .Result0(n1_bit_alu_1_result0[13]), .Carry0(n1_bit_alu_14_carry0), .Operand_B(Operand_B[13]),
    .Operand_A(Operand_A[13]), .Binvert(Binvert), .Operation(Operation), .Carry_In(n1_bit_alu_13_carry0));
  _1_Bit_ALU u_1_bit_alu_15 (
    .Result0(n1_bit_alu_1_result0[14]), .Carry0(n1_bit_alu_15_carry0), .Operand_B(Operand_B[14]),
    .Operand_A(Operand_A[14]), .Binvert(Binvert), .Operation(Operation), .Carry_In(n1_bit_alu_14_carry0));
  _1_Bit_ALU u_1_bit_alu_16 (
    .Result0(n1_bit_alu_1_result0[15]), .Carry0(Carry15), .Operand_B(Operand_B[15]),
    .Operand_A(Operand_A[15]), .Binvert(Binvert), .Operation(Operation), .Carry_In(n1_bit_alu_15_carry0));
  xor xor_1 (Overflow, n1_bit_alu_15_carry0, Carry15);
  Multiplexer #(.width(16), .enable("false")) multiplexer_1 (
    .in0(n1_bit_alu_1_result0), .in1({16{1'b0}}), .out(result), .sel(and_1_out));
  nor nor_1 (zero, n1_bit_alu_1_result0[0], n1_bit_alu_1_result0[1], n1_bit_alu_1_result0[2], n1_bit_alu_1_result0[3], n1_bit_alu_1_result0[4], n1_bit_alu_1_result0[5], n1_bit_alu_1_result0[6], n1_bit_alu_1_result0[7], n1_bit_alu_1_result0[8], n1_bit_alu_1_result0[9], n1_bit_alu_1_result0[10], n1_bit_alu_1_result0[11], n1_bit_alu_1_result0[12], n1_bit_alu_1_result0[13], n1_bit_alu_1_result0[14], n1_bit_alu_1_result0[15]);

  // Other names for the same wires on the sheet: A0 = Operand_A[0]; A1 = Operand_A[1]; A2 = Operand_A[2];
  //   A3 = Operand_A[3]; A4 = Operand_A[4]; A5 = Operand_A[5]; A6 = Operand_A[6]; A7 = Operand_A[7];
  //   A8 = Operand_A[8]; A9 = Operand_A[9]; A10 = Operand_A[10]; A11 = Operand_A[11]; A12 = Operand_A[12];
  //   A13 = Operand_A[13]; A14 = Operand_A[14]; A15 = Operand_A[15]; B0 = Operand_B[0]; B1 = Operand_B[1];
  //   B2 = Operand_B[2]; B3 = Operand_B[3]; B4 = Operand_B[4]; B5 = Operand_B[5]; B6 = Operand_B[6];
  //   B7 = Operand_B[7]; B8 = Operand_B[8]; B9 = Operand_B[9]; B10 = Operand_B[10]; B11 = Operand_B[11];
  //   B12 = Operand_B[12]; B13 = Operand_B[13]; B14 = Operand_B[14]; B15 = Operand_B[15]
endmodule

module Control (
  input  Sign_A,
  input  Sign_B,
  output Invert
);

  xor xor_1 (Invert, Sign_A, Sign_B);
endmodule

module Sign_Control (
  input  Sign_A,
  input  Sign_B,
  input  Number_A___Number_B,
  output Output_Sign
);

  wire xor_1_out;

  xor xor_1 (xor_1_out, Sign_B, 1'b0);
  Multiplexer #(.disabled(0), .enable("false")) multiplexer_1 (
    .in0(Sign_A), .in1(xor_1_out), .out(Output_Sign), .sel(Number_A___Number_B));
endmodule

module Bit_inverter (
  input  Control,
  input  [14:0] Input,
  output [15:0] Output
);

  wire [15:0] xor_1_out;

  assign xor_1_out = {16{Control}} ^ {1'b0, Input};  // XOR_Gate xor_1, 16 bits wide
  Adder #(.width(16)) adder_1 (.a({16{1'b0}}), .b(xor_1_out), .out(Output), .cin(Control));  // open: cout
endmodule

module Normalization (
  input  [3:0] Exponent_In,
  input  [15:0] in_2,
  output [3:0] Exponent_Out,
  output [15:0] out_4,
  output Underflow,
  output Overflow
);

  wire and_1_out, and_2_out, and_3_out, bitfinder_1_found, comparator_1_eq, comparator_1_gt, comparator_1_lt,
       not_1_out, or_1_out, or_3_out, subtractor_1_bout;
  wire [3:0] adder_1_out, bit_extender_1_out, bitfinder_1_index, multiplexer_1_out, multiplexer_2_out,
       multiplexer_5_out, multiplexer_6_out, subtractor_1_out, subtractor_2_out;
  wire [15:0] shifter_1_out, shifter_2_out;

  or or_1 (or_1_out, Exponent_In[0], Exponent_In[1], Exponent_In[2], Exponent_In[3]);
  Subtractor #(.width(4)) subtractor_1 (
    .a(Exponent_In), .b(subtractor_2_out), .out(subtractor_1_out), .bin(1'b0), .bout(subtractor_1_bout));
  Multiplexer #(.width(4), .enable("false")) multiplexer_1 (
    .in0(subtractor_1_out), .in1(4'b0000), .out(multiplexer_1_out), .sel(subtractor_1_bout));
  and and_1 (and_1_out, Exponent_In[3], Exponent_In[2], Exponent_In[0], Exponent_In[1]);
  Adder #(.width(4)) adder_1 (.a(Exponent_In), .b(4'b0000), .out(adder_1_out), .cin(and_2_out));  // open: cout
  Multiplexer #(.width(4), .enable("false")) multiplexer_2 (
    .in0(multiplexer_1_out), .in1(adder_1_out), .out(multiplexer_2_out), .sel(and_2_out));
  Multiplexer #(.width(4), .enable("false")) multiplexer_3 (
    .in0(4'b0000), .in1(multiplexer_2_out), .out(Exponent_Out), .sel(bitfinder_1_found));
  and and_2 (and_2_out, 1'b1, in_2[15]);
  assign bit_extender_1_out = {{3{1'b0}}, and_2_out};  // Bit_Extender bit_extender_1
  and and_3 (and_3_out, Exponent_Out[3], Exponent_Out[2], Exponent_Out[1], Exponent_Out[0]);
  or or_2 (Overflow, and_3_out, and_1_out);
  Shifter #(.width(16), .shift("lr")) shifter_1 (.in(in_2), .\dist (bit_extender_1_out), .out(shifter_1_out));
  Multiplexer #(.width(16), .enable("false")) multiplexer_4 (
    .in0(shifter_2_out), .in1(shifter_1_out), .out(out_4), .sel(and_2_out));
  not not_1 (not_1_out, and_2_out);
  BitFinder #(.width(16), .\type ("high1")) bitfinder_1 (
    .in(in_2), .index(bitfinder_1_index), .found(bitfinder_1_found));
  Multiplexer #(.width(4), .enable("false")) multiplexer_5 (
    .in0(4'b0000), .in1(4'b1110), .out(multiplexer_5_out), .sel(bitfinder_1_found));
  Comparator #(.width(4), .mode("unsigned")) comparator_1 (
    .a(Exponent_In), .b(subtractor_2_out), .gt(comparator_1_gt), .eq(comparator_1_eq), .lt(comparator_1_lt));
  and and_4 (Underflow, not_1_out, or_1_out, or_3_out);
  Subtractor #(.width(4)) subtractor_2 (
    .a(multiplexer_5_out), .b(bitfinder_1_index), .out(subtractor_2_out), .bin(1'b0));  // open: bout
  or or_3 (or_3_out, comparator_1_lt, comparator_1_eq);
  Multiplexer #(.width(4), .enable("false")) multiplexer_6 (
    .in0(4'b0000), .in1(subtractor_2_out), .out(multiplexer_6_out), .sel(comparator_1_gt));
  Shifter #(.width(16)) shifter_2 (.in(in_2), .\dist (multiplexer_6_out), .out(shifter_2_out));

  // Notes on the sheet:
  //   Significand In
  //   Significand Out
endmodule

module Rounding_circuit (
  input  [3:0] Exponent_In,
  input  [15:0] in_2,
  output [3:0] Exponent_Out,
  output [10:0] out_4,
  output Overflow
);

  wire and_1_out, and_3_out, or_1_out;
  wire [3:0] adder_1_out, bit_extender_1_out;
  wire [12:0] adder_2_out;
  wire [12:11] shifter_1_out;

  Multiplexer #(.width(4), .enable("false")) multiplexer_1 (
    .in0(Exponent_In), .in1(adder_1_out), .out(Exponent_Out), .sel(adder_2_out[12]));
  Adder #(.width(4)) adder_1 (.a(Exponent_In), .b(4'b0000), .out(adder_1_out), .cin(1'b1));  // open: cout
  and and_1 (and_1_out, Exponent_Out[0], Exponent_Out[1], Exponent_Out[2], Exponent_Out[3]);
  assign bit_extender_1_out = {{3{1'b0}}, adder_2_out[12]};  // Bit_Extender bit_extender_1
  and and_2 (Overflow, and_1_out, adder_2_out[12]);
  or or_1 (or_1_out, in_2[1], in_2[0]);
  and and_3 (and_3_out, in_2[2], or_1_out);
  Adder #(.width(13)) adder_2 (.a(in_2[15:3]), .b({13{1'b0}}), .out(adder_2_out), .cin(and_3_out));  // open: cout
  Shifter #(.width(13), .shift("lr")) shifter_1 (
    .in(adder_2_out), .\dist (bit_extender_1_out), .out({shifter_1_out, out_4}));

  // Notes on the sheet:
  //   Significand In
  //   Significand Out
endmodule

module FP_adder (
  input  [15:0] Operand_A,
  input  [15:0] Operand_B,
  output Underflow,
  output Overflow,
  output [15:0] Result
);

  wire comparator_1_eq, comparator_1_gt, comparator_1_lt, control_1_invert, normalization_1_overflow,
       or_1_out, or_3_out, rounding_circuit_1_overflow;
  wire [3:0] multiplexer_1_out, n4_bit_alu_1_exp__difff, normalization_1_exponent_out;
  wire [10:0] multiplexer_3_out;
  wire [14:0] shifter_1_out;
  wire [14:3] multiplexer_5_out;
  wire [14:14] multiplexer_2_out;
  wire [15:0] bit_inverter_1_output, n16_bit_alu_1_result, normalization_1_out_4;

  Sign_Control sign_control_1 (
    .Sign_A(Operand_A[15]), .Sign_B(Operand_B[15]), .Number_A___Number_B(comparator_1_lt),
    .Output_Sign(Result[15]));
  Control control_1 (.Sign_A(Operand_A[15]), .Sign_B(Operand_B[15]), .Invert(control_1_invert));
  Multiplexer #(.width(4), .enable("false")) multiplexer_1 (
    .in0(Operand_A[14:11]), .in1(Operand_B[14:11]), .out(multiplexer_1_out), .sel(comparator_1_lt));
  _4_bit_ALU u_4_bit_alu_1 (
    .CarryIn(1'b0), .A(Operand_A[14:11]), .B(Operand_B[14:11]), .Exp__Difff(n4_bit_alu_1_exp__difff),
    .BInvert(comparator_1_gt), .Operation(2'b10), .AInvert(comparator_1_lt), .A_B(comparator_1_eq));  // open: Zero, Overflow, Carry
  Rounding_circuit rounding_circuit_1 (
    .Exponent_In(normalization_1_exponent_out), .in_2(normalization_1_out_4), .Exponent_Out(Result[14:11]),
    .out_4(Result[10:0]), .Overflow(rounding_circuit_1_overflow));
  Normalization normalization_1 (
    .Exponent_In(multiplexer_1_out), .in_2(n16_bit_alu_1_result),
    .Exponent_Out(normalization_1_exponent_out), .Underflow(Underflow), .Overflow(normalization_1_overflow),
    .out_4(normalization_1_out_4));
  or or_1 (or_1_out, Operand_A[11], Operand_A[12], Operand_A[13], Operand_A[14]);
  Comparator #(.width(15), .mode("unsigned")) comparator_1 (
    .a(Operand_A[14:0]), .b(Operand_B[14:0]), .gt(comparator_1_gt), .eq(comparator_1_eq), .lt(comparator_1_lt));
  Multiplexer #(.enable("false")) multiplexer_2 (
    .in0(or_1_out), .in1(or_3_out), .out(multiplexer_2_out[14]), .sel(comparator_1_gt));
  Multiplexer #(.width(11), .enable("false")) multiplexer_3 (
    .in0(Operand_A[10:0]), .in1(Operand_B[10:0]), .out(multiplexer_3_out), .sel(comparator_1_gt));
  Shifter #(.width(15), .shift("lr")) shifter_1 (
    .in({multiplexer_2_out[14], multiplexer_3_out, 3'b000}), .\dist (n4_bit_alu_1_exp__difff),
    .out(shifter_1_out));
  or or_2 (Overflow, normalization_1_overflow, rounding_circuit_1_overflow);
  or or_3 (or_3_out, Operand_B[14], Operand_B[13], Operand_B[12], Operand_B[11]);
  Multiplexer #(.enable("false")) multiplexer_4 (
    .in0(or_3_out), .in1(or_1_out), .out(multiplexer_5_out[14]), .sel(comparator_1_gt));
  Bit_inverter bit_inverter_1 (.Control(control_1_invert), .Input(shifter_1_out), .Output(bit_inverter_1_output));
  Multiplexer #(.width(11), .enable("false")) multiplexer_5 (
    .in0(Operand_A[10:0]), .in1(Operand_B[10:0]), .out(multiplexer_5_out[13:3]), .sel(comparator_1_lt));
  _16_bit_ALU u_16_bit_alu_1 (
    .Operand_A({1'b0, multiplexer_5_out, 3'b000}), .Operand_B(bit_inverter_1_output), .Operation(2'b10),
    .Binvert(1'b0), .result(n16_bit_alu_1_result), .CarryIn(1'b0), .A_B(comparator_1_eq));  // open: Carry15, Overflow, zero

  // Notes on the sheet:
  //   Shifter
endmodule
